// Logisim project processor.circ as structural Verilog: 16 circuits, main circuit processor
module processor (
  output [15:0] R0,
  output [15:0] R1
);

  wire alu_1_carry, alu_1_zero, branch_1_jmp, brk_1_clkout, button_1_out, control_1_absjmp,
       control_1_alustore, control_1_brk, control_1_immstore, control_1_iowrite, control_1_ld,
       control_1_sourcetoalu, control_1_st_pc, control_1_str, control_1_we, terminal_1_termtakt;
  wire [2:0] control_1_branch, control_1_immediate;
  wire [4:0] control_1_alu_ctrl;
  wire [6:0] terminal_1_ascii;
  wire [15:0] alu_1_out, graphic_1_out_5, graphic_1_out_6, graphic_1_out_7, graphic_1_out_8, graphic_1_out_9,
       graphic_1_out_10, graphic_1_out_11, graphic_1_out_12, graphic_1_out_13, graphic_1_out_14,
       graphic_1_out_15, graphic_1_out_16, graphic_1_out_17, graphic_1_out_18, graphic_1_out_19,
       graphic_1_out_20, imReg_imediate, multiplexer_1_out, multiplexer_2_out, multiplexer_3_out,
       multiplexer_4_out, pc_logic_1_act_pc, pc_logic_1_next_seq_pc, ram_1_data, registers_1_dest_2,
       registers_1_source_2, rom_1_data, SignExtend__5_bit_dest, SignExtend__5_bit_source, SignExtend__9_bit;

  TTY #(.rows(20)) tty_1 (.data(terminal_1_ascii), .clk(terminal_1_termtakt));  // open: we, clr
  PC_logic pc_logic_1 (
    .ALU_out(alu_1_out), .act_PC(pc_logic_1_act_pc), .next_seq_PC(pc_logic_1_next_seq_pc),
    .Takt(brk_1_clkout), .rel__jmp(branch_1_jmp), .abs__jmp(control_1_absjmp));
  LED led_1 (.in(control_1_brk));
  Button button_1 (.out(button_1_out));
  brk brk_1 (.BRK(control_1_brk), .clkout(brk_1_clkout), .Taster(button_1_out));
  ROM #(.addrWidth(16), .dataWidth(16)) rom_1 (.addr(pc_logic_1_act_pc), .data(rom_1_data));  // open: sel
  Multiplexer #(.width(16), .enable("false")) multiplexer_1 (
    .in0(multiplexer_2_out), .in1(pc_logic_1_next_seq_pc), .out(multiplexer_1_out), .sel(control_1_st_pc));
  imReg imReg (.instruction(rom_1_data), .En(control_1_immstore), .Takt(brk_1_clkout), .imediate(imReg_imediate));
  control control_1 (
    .Opcode(rom_1_data[15:9]), .WE(control_1_we), .ALUStore(control_1_alustore),
    .immediate(control_1_immediate), .ALU_ctrl(control_1_alu_ctrl), .branch(control_1_branch),
    .str(control_1_str), .ld(control_1_ld), .ST_PC(control_1_st_pc), .SourceToAlu(control_1_sourcetoalu),
    .ImmStore(control_1_immstore), .AbsJmp(control_1_absjmp), .ioWrite(control_1_iowrite), .BRK(control_1_brk));  // open: ioRead
  Multiplexer #(.width(16), .enable("false")) multiplexer_2 (
    .in0(ram_1_data), .in1(alu_1_out), .out(multiplexer_2_out), .sel(control_1_alustore));
  registers registers_1 (
    .Write(multiplexer_1_out), .dest_2(registers_1_dest_2), .source_2(registers_1_source_2),
    .WE(control_1_we), .dest(rom_1_data[7:4]), .Clock(brk_1_clkout), .R0(R0), .R1(R1),
    .source(rom_1_data[3:0]));
  SignExtend SignExtend (
    .Instruction(rom_1_data), ._9_Bit(SignExtend__9_bit), ._5_Bit_Dest(SignExtend__5_bit_dest),
    ._5_Bit_Source(SignExtend__5_bit_source));
  Multiplexer #(.select(3), .width(16), .enable("false")) multiplexer_3 (
    .in0(registers_1_source_2), .in1(imReg_imediate), .in2({16{1'b0}}), .in3(16'h1), .in4(16'h2),
    .in5(SignExtend__5_bit_source), .in6(SignExtend__9_bit), .in7(SignExtend__5_bit_dest),
    .out(multiplexer_3_out), .sel(control_1_immediate));
  Multiplexer #(.width(16), .enable("false")) multiplexer_4 (
    .in0(registers_1_dest_2), .in1(registers_1_source_2), .out(multiplexer_4_out), .sel(control_1_sourcetoalu));
  ALU alu_1 (
    .A(multiplexer_4_out), .B(multiplexer_3_out), .Out(alu_1_out), .Zero(alu_1_zero), .Carry(alu_1_carry),
    .Takt(brk_1_clkout), .SelOp(control_1_alu_ctrl));
  branch branch_1 (.Kind(control_1_branch), .Jmp(branch_1_jmp), .C(alu_1_carry), .Z(alu_1_zero));
  terminal terminal_1 (
    .data(registers_1_source_2), .addr(alu_1_out), .ASCII(terminal_1_ascii), .TermTakt(terminal_1_termtakt),
    .io_Write(control_1_iowrite));
  RAM #(.addrWidth(16), .dataWidth(16), .bus("separate")) ram_1 (
    .addr(alu_1_out), .din(registers_1_source_2), .data(ram_1_data), .str(control_1_str), .clk(brk_1_clkout),
    .ld(control_1_ld));  // open: sel, clr
  DotMatrix #(.matrixcols(16), .matrixrows(16)) dotmatrix_1 (
    .col0(graphic_1_out_5), .col1(graphic_1_out_6), .col2(graphic_1_out_7), .col3(graphic_1_out_8),
    .col4(graphic_1_out_9), .col5(graphic_1_out_10), .col6(graphic_1_out_11), .col7(graphic_1_out_12),
    .col8(graphic_1_out_13), .col9(graphic_1_out_14), .col10(graphic_1_out_15), .col11(graphic_1_out_16),
    .col12(graphic_1_out_17), .col13(graphic_1_out_18), .col14(graphic_1_out_19), .col15(graphic_1_out_20));
  graphic graphic_1 (
    .Data(registers_1_source_2), .Takt(brk_1_clkout), .Enable(control_1_iowrite), .Addr(alu_1_out),
    .out_5(graphic_1_out_5), .out_6(graphic_1_out_6), .out_7(graphic_1_out_7), .out_8(graphic_1_out_8),
    .out_9(graphic_1_out_9), .out_10(graphic_1_out_10), .out_11(graphic_1_out_11), .out_12(graphic_1_out_12),
    .out_13(graphic_1_out_13), .out_14(graphic_1_out_14), .out_15(graphic_1_out_15),
    .out_16(graphic_1_out_16), .out_17(graphic_1_out_17), .out_18(graphic_1_out_18),
    .out_19(graphic_1_out_19), .out_20(graphic_1_out_20));

  // Notes on the sheet:
  //   Programm
  //   contents of rom_1 (hex, n*v repeats v):
  //   1400 5260 5320 8020 1200 5250 52a0 8021 1200 5310 8061 1200 5270 52c0 8064 1200 5300 8065 1200 5200
  //   52f0 806c 1200 5280 5290 806f 1200 5230 8070 1200 52b0 8072 1200 5210 5220 5240 8073 1200 52d0 52e0
  //   1470 1000 1405 3c05 6001 5c7d 3c04 6401 5c7a 3c04 6401 5c77 1471 1407 1415 401 3c0c 6001 5c70 150e
  //   151e 401 803c 3a00 6001 5c69 1472 1407 1415 801 3c02 6001 5c62 8023 1200 8021 1210 801 3c02 6001
  //   5c5a 1473 1407 1415 1421 4020 601 3c0d 6001 5c51 1474 1407 1415 1421 4020 a01 3c01 6001 5c48 1475
  //   ffff 1300 4600 ffff 3b00 6001 5c40 ffff 1200 4600 bfff 3a00 6001 5c39 1401 4600 5e01 5c35 4600 6201
  //   5c32 1476 9234 1200 4800 b412 3a00 6001 5c2a 9234 1200 4a00 a143 3a00 6001 5c23 1477 808b 6600 808b
  //   1210 3810 6001 5c1b 1478 1407 3603 3d05 6001 5c15 1407 8028 3400 8118 3a00 6001 5c0e 1407 1413 3201
  //   3d05 6001 5c08 1407 20f1 4cfe 80bb 66e0 4eef 18f1 5dff 1400 20f1 4cfe 80bb 66e0 4eef 18f1 207 20f1
  //   4cfe 80c1 66e0 4eef 18f1 7a00 5dff 4e10 6ff1 1801 3c10 65fb 680e 4800 4a00 80d0 6620 4a00 80d0 6620
  //   4800 4a00 80d0 6620 4a00 80d0 6620 680e 210 281f 3c1a 6203 8030 1610 5c02 8037 1610 6ff1 6802
  //   RAM
endmodule

module registers (
  input  [15:0] Write,
  input  [3:0] source,
  input  WE,
  input  [3:0] dest,
  input  Clock,
  output [15:0] R0,
  output [15:0] R1,
  output [15:0] dest_2,
  output [15:0] source_2
);

  wire demultiplexer_1_out0, demultiplexer_1_out1, demultiplexer_1_out2, demultiplexer_1_out3,
       demultiplexer_1_out4, demultiplexer_1_out5, demultiplexer_1_out6, demultiplexer_1_out7,
       demultiplexer_1_out8, demultiplexer_1_out9, demultiplexer_1_out10, demultiplexer_1_out11,
       demultiplexer_1_out12, demultiplexer_1_out13, demultiplexer_1_out14, demultiplexer_1_out15;
  wire [15:0] R0_2_q, R1_2_q, R2_2_q, R2_q, R3_2_q, R3_q, R4_2_q, R4_q, R5_2_q, R5_q, R6_2_q, R6_q, R7_2_q,
       R7_q;

  Demultiplexer #(.select(4), .enable("false")) demultiplexer_1 (
    .out0(demultiplexer_1_out0), .out1(demultiplexer_1_out1), .out2(demultiplexer_1_out2),
    .out3(demultiplexer_1_out3), .out4(demultiplexer_1_out4), .out5(demultiplexer_1_out5),
    .out6(demultiplexer_1_out6), .out7(demultiplexer_1_out7), .out8(demultiplexer_1_out8),
    .out9(demultiplexer_1_out9), .out10(demultiplexer_1_out10), .out11(demultiplexer_1_out11),
    .out12(demultiplexer_1_out12), .out13(demultiplexer_1_out13), .out14(demultiplexer_1_out14),
    .out15(demultiplexer_1_out15), .in(WE), .sel(dest));
  Register #(.width(16)) u_R0 (.D(Write), .en(demultiplexer_1_out0), .Q(R0), .clk(Clock));  // open: clr
  Register #(.width(16)) u_R1 (.D(Write), .en(demultiplexer_1_out1), .Q(R1), .clk(Clock));  // open: clr
  Register #(.width(16)) R2 (.D(Write), .en(demultiplexer_1_out2), .Q(R2_q), .clk(Clock));  // open: clr
  Register #(.width(16)) R3 (.D(Write), .en(demultiplexer_1_out3), .Q(R3_q), .clk(Clock));  // open: clr
  Register #(.width(16)) R4 (.D(Write), .en(demultiplexer_1_out4), .Q(R4_q), .clk(Clock));  // open: clr
  Register #(.width(16)) R5 (.D(Write), .en(demultiplexer_1_out5), .Q(R5_q), .clk(Clock));  // open: clr
  Register #(.width(16)) R6 (.D(Write), .en(demultiplexer_1_out6), .Q(R6_q), .clk(Clock));  // open: clr
  Register #(.width(16)) R7 (.D(Write), .en(demultiplexer_1_out7), .Q(R7_q), .clk(Clock));  // open: clr
  Register #(.width(16)) R0_2 (.D(Write), .en(demultiplexer_1_out8), .Q(R0_2_q), .clk(Clock));  // open: clr
  Register #(.width(16)) R1_2 (.D(Write), .en(demultiplexer_1_out9), .Q(R1_2_q), .clk(Clock));  // open: clr
  Register #(.width(16)) R2_2 (.D(Write), .en(demultiplexer_1_out10), .Q(R2_2_q), .clk(Clock));  // open: clr
  Register #(.width(16)) R3_2 (.D(Write), .en(demultiplexer_1_out11), .Q(R3_2_q), .clk(Clock));  // open: clr
  Register #(.width(16)) R4_2 (.D(Write), .en(demultiplexer_1_out12), .Q(R4_2_q), .clk(Clock));  // open: clr
  Register #(.width(16)) R5_2 (.D(Write), .en(demultiplexer_1_out13), .Q(R5_2_q), .clk(Clock));  // open: clr
  Register #(.width(16)) R6_2 (.D(Write), .en(demultiplexer_1_out14), .Q(R6_2_q), .clk(Clock));  // open: clr
  Register #(.width(16)) R7_2 (.D(Write), .en(demultiplexer_1_out15), .Q(R7_2_q), .clk(Clock));  // open: clr
  Multiplexer #(.select(4), .width(16), .enable("false")) multiplexer_1 (
    .in0(R0), .in1(R1), .in2(R2_q), .in3(R3_q), .in4(R4_q), .in5(R5_q), .in6(R6_q), .in7(R7_q), .in8(R0_2_q),
    .in9(R1_2_q), .in10(R2_2_q), .in11(R3_2_q), .in12(R4_2_q), .in13(R5_2_q), .in14(R6_2_q), .in15(R7_2_q),
    .out(dest_2), .sel(dest));
  Multiplexer #(.select(4), .width(16), .enable("false")) multiplexer_2 (
    .in0(R0), .in1(R1), .in2(R2_q), .in3(R3_q), .in4(R4_q), .in5(R5_q), .in6(R6_q), .in7(R7_q), .in8(R0_2_q),
    .in9(R1_2_q), .in10(R2_2_q), .in11(R3_2_q), .in12(R4_2_q), .in13(R5_2_q), .in14(R6_2_q), .in15(R7_2_q),
    .out(source_2), .sel(source));
endmodule

module ALU (
  input  [15:0] A,
  input  [15:0] B,
  input  Takt,
  input  [4:0] SelOp,
  output [15:0] Out,
  output Zero,
  output Carry
);

  wire adder_1_cout, and_2_out, asr_1_lsb_out, comparator_1_eq, lsl_1_msb_out, lsr_1_lsb_out,
       multiplexer_1_out, multiplexer_2_out, subtractor_1_bout;
  wire [15:0] adder_1_out, and_1_out, asr_1_out, lsl_1_out, lsr_1_out, multiplier_1_out, or_1_out,
       subtractor_1_out, swap_1_out, swapn_1_out, xor_1_out;

  Adder #(.width(16)) adder_1 (.a(A), .b(B), .out(adder_1_out), .cin(and_2_out), .cout(adder_1_cout));
  Subtractor #(.width(16)) subtractor_1 (
    .a(A), .b(B), .out(subtractor_1_out), .bin(and_2_out), .bout(subtractor_1_bout));
  assign and_1_out = A & B;  // AND_Gate and_1, 16 bits wide
  assign or_1_out = A | B;  // OR_Gate or_1, 16 bits wide
  assign xor_1_out = A ^ B;  // XOR_Gate xor_1, 16 bits wide
  LSL lsl_1 (.LSB_In(and_2_out), .Data(A), .Out(lsl_1_out), .MSB_Out(lsl_1_msb_out));
  LSR lsr_1 (.Data(A), .MSB_In(and_2_out), .LSB_Out(lsr_1_lsb_out), .Out(lsr_1_out));
  ASR asr_1 (.Data(A), .LSB_Out(asr_1_lsb_out), .Out(asr_1_out));
  swap swap_1 (.Data(A), .Out(swap_1_out));
  swapN swapn_1 (.Data(A), .Out(swapn_1_out));
  Multiplier #(.width(16)) multiplier_1 (.a(A), .b(B), .out(multiplier_1_out));  // open: cin, cout
  and and_2 (and_2_out, SelOp[4], Carry);
  Multiplexer #(.select(4), .enable("false")) multiplexer_1 (
    .in0(Carry), .in1(adder_1_cout), .in2(subtractor_1_bout), .in3(Carry), .in4(Carry), .in5(Carry),
    .in6(lsl_1_msb_out), .in7(lsr_1_lsb_out), .in8(asr_1_lsb_out), .in9(Carry), .in10(Carry), .in11(Carry),
    .in12(Carry), .in13(Carry), .in14(Carry), .in15(Carry), .out(multiplexer_1_out), .sel(SelOp[3:0]));
  Multiplexer #(.select(4), .enable("false")) multiplexer_2 (
    .in0(1'b0), .in1(1'b1), .in2(1'b1), .in3(1'b0), .in4(1'b0), .in5(1'b0), .in6(1'b1), .in7(1'b1),
    .in8(1'b1), .in9(1'b0), .in10(1'b0), .in11(1'b0), .in12(1'b0), .in13(1'b0), .in14(1'b0), .in15(1'b0),
    .out(multiplexer_2_out), .sel(SelOp[3:0]));
  D_Flip_Flop u_Carry (
    .clk(Takt), .D(multiplexer_1_out), .Q(Carry), .en(multiplexer_2_out));  // open: Qn, preset, reset
  Multiplexer #(.select(4), .width(16), .enable("false")) multiplexer_3 (
    .in0(B), .in1(adder_1_out), .in2(subtractor_1_out), .in3(and_1_out), .in4(or_1_out), .in5(xor_1_out),
    .in6(lsl_1_out), .in7(lsr_1_out), .in8(asr_1_out), .in9(swap_1_out), .in10(swapn_1_out),
    .in11(multiplier_1_out), .out(Out), .sel(SelOp[3:0]));  // open: in12, in13, in14, in15
  Comparator #(.width(16)) comparator_1 (.a(Out), .b({16{1'b0}}), .eq(comparator_1_eq));  // open: gt, lt
  D_Flip_Flop u_Zero (.clk(Takt), .D(comparator_1_eq), .Q(Zero), .en(multiplexer_2_out));  // open: Qn, preset, reset
endmodule

module LSL (
  input  LSB_In,
  input  [15:0] Data,
  output [15:0] Out,
  output MSB_Out
);


  assign MSB_Out = Data[15];
  assign Out = {Data[14:0], LSB_In};
endmodule

module LSR (
  input  [15:0] Data,
  input  MSB_In,
  output LSB_Out,
  output [15:0] Out
);


  assign LSB_Out = Data[0];
  assign Out = {MSB_In, Data[15:1]};
endmodule

module ASR (
  input  [15:0] Data,
  output LSB_Out,
  output [15:0] Out
);


  assign LSB_Out = Data[0];
  assign Out = {{2{Data[15]}}, Data[14:1]};
endmodule

module swap (
  input  [15:0] Data,
  output [15:0] Out
);


  assign Out = {Data[7:0], Data[15:8]};
endmodule

module swapN (
  input  [15:0] Data,
  output [15:0] Out
);


  assign Out = {Data[11:8], Data[15:12], Data[3:0], Data[7:4]};
endmodule

module branch (
  input  C,
  input  Z,
  input  [2:0] Kind,
  output Jmp
);

  wire multiplexer_1_out;

  Multiplexer #(.select(2), .enable("false")) multiplexer_1 (
    .in0(1'b0), .in1(C), .in2(Z), .in3(1'b1), .out(multiplexer_1_out), .sel(Kind[1:0]));
  xor xor_1 (Jmp, multiplexer_1_out, Kind[2]);
endmodule

module control (
  input  [6:0] Opcode,
  output ImmStore,
  output AbsJmp,
  output SourceToAlu,
  output ALUStore,
  output [2:0] immediate,
  output [4:0] ALU_ctrl,
  output WE,
  output [2:0] branch,
  output ST_PC,
  output str,
  output ld,
  output ioWrite,
  output ioRead,
  output BRK
);

  wire [5:0] multiplexer_1_out;
  wire [23:21] rom_1_data;

  Multiplexer #(.width(6), .enable("false")) multiplexer_1 (
    .in0(Opcode[5:0]), .in1({6{1'b0}}), .out(multiplexer_1_out), .sel(Opcode[6]));
  ROM #(.addrWidth(6), .dataWidth(24)) rom_1 (
    .addr(multiplexer_1_out),
    .data({rom_1_data, BRK, ioRead, ioWrite, branch, ALU_ctrl, SourceToAlu, ST_PC, WE, ALUStore, AbsJmp, immediate, str, ld}));  // open: sel

  assign ImmStore = Opcode[6];

  // Notes on the sheet:
  //   contents of rom_1 (hex, n*v repeats v):
  //   0 c0 4c0 44c0 8c0 48c0 cc0 10c0 14c0 c4 d4 4c4 4d4 44c4 44d4 8c4 8d4 48c4 48d4 cc4 cd4 10c4 10d4
  //   14c4 14d4 2cc0 2cc4 2cd4 840 844 854 18c0 1cc0 58c0 5cc0 20c0 24c0 28c0 44a 689 46 5e 85 95 446 685
  //   18018 8018 10018 28018 30018 1a4 20 24 40044 4005c 40444 40448 80284 80684 80688 100000
endmodule

module PC_logic (
  input  [15:0] ALU_out,
  input  Takt,
  input  rel__jmp,
  input  abs__jmp,
  output [15:0] next_seq_PC,
  output [15:0] act_PC
);

  wire [15:0] adder_2_out, multiplexer_1_out, multiplexer_2_out;

  Register #(.width(16)) PC (.D(multiplexer_2_out), .Q(act_PC), .clk(Takt));  // open: en, clr
  Adder #(.width(16)) adder_1 (.a(act_PC), .b(16'h1), .out(next_seq_PC));  // open: cin, cout
  Adder #(.width(16)) adder_2 (.a(next_seq_PC), .b(ALU_out), .out(adder_2_out));  // open: cin, cout
  Multiplexer #(.width(16), .enable("false")) multiplexer_1 (
    .in0(next_seq_PC), .in1(adder_2_out), .out(multiplexer_1_out), .sel(rel__jmp));
  Multiplexer #(.width(16), .enable("false")) multiplexer_2 (
    .in0(multiplexer_1_out), .in1(ALU_out), .out(multiplexer_2_out), .sel(abs__jmp));

  // Notes on the sheet:
  //   rel__jmp: pull=down
  //   abs__jmp: pull=down
endmodule

module imReg (
  input  [15:0] instruction,
  input  En,
  input  Takt,
  output [15:0] imediate
);

  wire [15:15] register_1_q;

  Register #(.width(16)) register_1 (
    .D(instruction), .en(En), .Q({register_1_q[15], imediate[14:0]}), .clk(Takt));  // open: clr

  assign imediate[15] = instruction[8];
endmodule

module SignExtend (
  input  [15:0] Instruction,
  output [15:0] _9_Bit,
  output [15:0] _5_Bit_Dest,
  output [15:0] _5_Bit_Source
);


  assign _5_Bit_Dest = {{11{1'b0}}, Instruction[8:4]};
  assign _5_Bit_Source = {{11{1'b0}}, Instruction[8], Instruction[3:0]};
  assign _9_Bit = {{8{Instruction[8]}}, Instruction[7:0]};
endmodule

module brk (
  input  Taster,
  input  BRK,
  output clkout
);

  wire and_1_out, clock_1_out, not_1_out;

  Clock clock_1 (.out(clock_1_out));
  not not_1 (not_1_out, BRK);
  and and_1 (and_1_out, clock_1_out, not_1_out);
  or or_1 (clkout, Taster, and_1_out);
endmodule

module graphic (
  input  [15:0] Data,
  input  Takt,
  input  Enable,
  input  [15:0] Addr,
  output [15:0] out_5,
  output [15:0] out_6,
  output [15:0] out_7,
  output [15:0] out_8,
  output [15:0] out_9,
  output [15:0] out_10,
  output [15:0] out_11,
  output [15:0] out_12,
  output [15:0] out_13,
  output [15:0] out_14,
  output [15:0] out_15,
  output [15:0] out_16,
  output [15:0] out_17,
  output [15:0] out_18,
  output [15:0] out_19,
  output [15:0] out_20
);

  wire demultiplexer_1_out0, demultiplexer_1_out1, demultiplexer_1_out2, demultiplexer_1_out3,
       demultiplexer_1_out4, demultiplexer_1_out5, demultiplexer_1_out6, demultiplexer_1_out7,
       demultiplexer_1_out8, demultiplexer_1_out9, demultiplexer_1_out10, demultiplexer_1_out11,
       demultiplexer_1_out12, demultiplexer_1_out13, demultiplexer_1_out14, demultiplexer_1_out15,
       demultiplexer_1_out16;
  wire [15:0] register_1_q, register_2_q, register_3_q, register_4_q, register_5_q, register_6_q,
       register_7_q, register_8_q, register_9_q, register_10_q, register_11_q, register_12_q, register_13_q,
       register_14_q, register_15_q, register_16_q;

  Demultiplexer #(.select(5), .enable("false")) demultiplexer_1 (
    .out0(demultiplexer_1_out0), .out1(demultiplexer_1_out1), .out2(demultiplexer_1_out2),
    .out3(demultiplexer_1_out3), .out4(demultiplexer_1_out4), .out5(demultiplexer_1_out5),
    .out6(demultiplexer_1_out6), .out7(demultiplexer_1_out7), .out8(demultiplexer_1_out8),
    .out9(demultiplexer_1_out9), .out10(demultiplexer_1_out10), .out11(demultiplexer_1_out11),
    .out12(demultiplexer_1_out12), .out13(demultiplexer_1_out13), .out14(demultiplexer_1_out14),
    .out15(demultiplexer_1_out15), .out16(demultiplexer_1_out16), .in(Enable), .sel(Addr[4:0]));  // open: out17, out18, out19, out20, out21, out22, out23, out24, out25, out26, out27, out28, out29, out30, out31
  Register #(.width(16)) register_1 (.D(Data), .en(demultiplexer_1_out0), .Q(register_1_q), .clk(Takt));  // open: clr
  Register #(.width(16)) register_2 (.D(Data), .en(demultiplexer_1_out1), .Q(register_2_q), .clk(Takt));  // open: clr
  Register #(.width(16)) register_3 (.D(Data), .en(demultiplexer_1_out2), .Q(register_3_q), .clk(Takt));  // open: clr
  Register #(.width(16)) register_4 (.D(Data), .en(demultiplexer_1_out3), .Q(register_4_q), .clk(Takt));  // open: clr
  Register #(.width(16)) register_5 (.D(Data), .en(demultiplexer_1_out4), .Q(register_5_q), .clk(Takt));  // open: clr
  Register #(.width(16)) register_6 (.D(Data), .en(demultiplexer_1_out5), .Q(register_6_q), .clk(Takt));  // open: clr
  Register #(.width(16)) register_7 (.D(Data), .en(demultiplexer_1_out6), .Q(register_7_q), .clk(Takt));  // open: clr
  Register #(.width(16)) register_8 (.D(Data), .en(demultiplexer_1_out7), .Q(register_8_q), .clk(Takt));  // open: clr
  Register #(.width(16)) register_9 (.D(Data), .en(demultiplexer_1_out8), .Q(register_9_q), .clk(Takt));  // open: clr
  Register #(.width(16)) register_10 (.D(Data), .en(demultiplexer_1_out9), .Q(register_10_q), .clk(Takt));  // open: clr
  Register #(.width(16)) register_11 (
    .D(Data), .en(demultiplexer_1_out10), .Q(register_11_q), .clk(Takt));  // open: clr
  Register #(.width(16)) register_12 (
    .D(Data), .en(demultiplexer_1_out11), .Q(register_12_q), .clk(Takt));  // open: clr
  Register #(.width(16)) register_13 (
    .D(Data), .en(demultiplexer_1_out12), .Q(register_13_q), .clk(Takt));  // open: clr
  Register #(.width(16)) register_14 (
    .D(Data), .en(demultiplexer_1_out13), .Q(register_14_q), .clk(Takt));  // open: clr
  Register #(.width(16)) register_15 (
    .D(Data), .en(demultiplexer_1_out14), .Q(register_15_q), .clk(Takt));  // open: clr
  Register #(.width(16)) register_16 (
    .D(Data), .en(demultiplexer_1_out15), .Q(register_16_q), .clk(Takt));  // open: clr
  Register #(.width(16)) register_17 (
    .D(register_1_q), .en(demultiplexer_1_out16), .Q(out_5), .clk(Takt));  // open: clr
  Register #(.width(16)) register_18 (
    .D(register_2_q), .en(demultiplexer_1_out16), .Q(out_6), .clk(Takt));  // open: clr
  Register #(.width(16)) register_19 (
    .D(register_3_q), .en(demultiplexer_1_out16), .Q(out_7), .clk(Takt));  // open: clr
  Register #(.width(16)) register_20 (
    .D(register_4_q), .en(demultiplexer_1_out16), .Q(out_8), .clk(Takt));  // open: clr
  Register #(.width(16)) register_21 (
    .D(register_5_q), .en(demultiplexer_1_out16), .Q(out_9), .clk(Takt));  // open: clr
  Register #(.width(16)) register_22 (
    .D(register_6_q), .en(demultiplexer_1_out16), .Q(out_10), .clk(Takt));  // open: clr
  Register #(.width(16)) register_23 (
    .D(register_7_q), .en(demultiplexer_1_out16), .Q(out_11), .clk(Takt));  // open: clr
  Register #(.width(16)) register_24 (
    .D(register_8_q), .en(demultiplexer_1_out16), .Q(out_12), .clk(Takt));  // open: clr
  Register #(.width(16)) register_25 (
    .D(register_9_q), .en(demultiplexer_1_out16), .Q(out_13), .clk(Takt));  // open: clr
  Register #(.width(16)) register_26 (
    .D(register_10_q), .en(demultiplexer_1_out16), .Q(out_14), .clk(Takt));  // open: clr
  Register #(.width(16)) register_27 (
    .D(register_11_q), .en(demultiplexer_1_out16), .Q(out_15), .clk(Takt));  // open: clr
  Register #(.width(16)) register_28 (
    .D(register_12_q), .en(demultiplexer_1_out16), .Q(out_16), .clk(Takt));  // open: clr
  Register #(.width(16)) register_29 (
    .D(register_13_q), .en(demultiplexer_1_out16), .Q(out_17), .clk(Takt));  // open: clr
  Register #(.width(16)) register_30 (
    .D(register_14_q), .en(demultiplexer_1_out16), .Q(out_18), .clk(Takt));  // open: clr
  Register #(.width(16)) register_31 (
    .D(register_15_q), .en(demultiplexer_1_out16), .Q(out_19), .clk(Takt));  // open: clr
  Register #(.width(16)) register_32 (
    .D(register_16_q), .en(demultiplexer_1_out16), .Q(out_20), .clk(Takt));  // open: clr
endmodule

// Term
module terminal (
  input  [15:0] data,
  input  [15:0] addr,
  input  io_Write,
  output [6:0] ASCII,
  output TermTakt
);

  wire comparator_1_eq;

  Comparator #(.width(16)) comparator_1 (.a(addr), .b(16'h1f), .eq(comparator_1_eq));  // open: gt, lt
  and and_1 (TermTakt, comparator_1_eq, io_Write);

  assign ASCII = data[6:0];
endmodule
